# Fritzing sketch homecage (saved by Fritzing 0.9.3b)

parts:
  Raspberry_Pi_1 = Raspberry Pi 3 [part_number=RPI-3-V1.2]  # not connected
  LED3 = LED - 3mm [color="White (4500K)" package="3 mm [THT]"]
  LED2 = LED - 3mm [color="Red (633nm)" package="3 mm [THT]"]
  U3 = 2-Channel 5v Relay Shield [package=relay-2ch5v10a]
  J1 = Power Jack [package=power_jack_smd]
  U2 = TMP102 [package=sot563]  # not connected

nets:
  N1: LED3.anode, U3.K2-On
  N2: LED2.cathode, J1.GNDBREAK
  N3: LED2.anode, U3.K1-On
  N4: U3.K1-In, U3.K2-In, J1.GND

custom parts:
  2-Channel 5v Relay Shield: 2 Channel 5v Relay Shield w. 2x SPD-06VDC-SD-C
